# Fritzing sketch simulation (saved by Fritzing 0.9.3b)
breadboards: 1

parts:
  Sensor = MAX30102
  PIEZO_(BUZZER) = Piezo Speaker
  Sensor_2 = LM35 Temperature Sensor [package="TO92 [THT]"]
  R1 = Resistor [tolerance=±5% resistance=27k package="0603 [SMD]"]
  NPN = NPN-Transistor [package="SOT-23 [SMD]"]
  Microcontroller = Arduino Uno (Rev3)
  R3 = Resistor [tolerance=±5% resistance=1k package="0603 [SMD]"]
  R2 = Resistor [tolerance=±5% resistance=1k package="0603 [SMD]"]

nets:
  VIN: Sensor.VIN, PIEZO_(BUZZER).pin2, Sensor_2.+Vs, Microcontroller.5V
  N1: Sensor.SCL, R3.Pin_0
  N2: Sensor.SDA, R2.Pin_0
  GND: Sensor.GND, Sensor_2.GND, NPN.1, Microcontroller.GND
  N3: PIEZO_(BUZZER).pin1, NPN.2
  N4: Sensor_2.Vout, Microcontroller.A0
  N5: R1.Pin_0, Microcontroller.D3_PWM
  N6: R1.Pin_1, NPN.0
  N7: Microcontroller.A4/SDA, R2.Pin_1
  N8: Microcontroller.A5/SCL, R3.Pin_1

notes:
  El valor de 1KOhm para las resistencias del MAX30102 lo hemos extraido del recomendado en el "data-sheet" elaborado por MaximIntegrated, TM.

custom parts:
  MAX30102: Oximeter module using the MAX30102 chip. You may wish to read (and check your module) this post on power problems with these modules: https://reedpaper.wordpress.com/2018/08/22/pulse-oximeter-max30100-max30102-how-to-fix-wrong-board/ . As usual, if you want the mounting holes in pcb, you need to drag a hole over the pad in silkscreen to actually drill the hole (by default they are not drilled)
